# Fritzing sketch Intro - robotics (saved by Fritzing 0.8.7b)
breadboards: 1

parts:
  QUAD_2_1_MUX = SELECTOR_MULTIPLEXER [package=dil16]
  DC_MOTOR_DRIVER = L298 [package=multiwatt15]
  CONTROLER_BOARD = Arduino Uno (Rev3)
  USER_BOARD = Arduino Uno (Rev3)
  MOTORS = female pin header, 4 pins [form="♀ (female)"]

nets:
  BOARD_SELECT: QUAD_2_1_MUX.A_!A!_B, CONTROLER_BOARD.D4
  N1: QUAD_2_1_MUX.A_1A, CONTROLER_BOARD.D5_PWM
  USR_DRV0A: QUAD_2_1_MUX.A_1B, USER_BOARD.D5_PWM
  DRV0_A: QUAD_2_1_MUX.A_1Y, DC_MOTOR_DRIVER.IN1
  N2: QUAD_2_1_MUX.A_2A, CONTROLER_BOARD.D6_PWM
  USR_DRV0B: QUAD_2_1_MUX.A_2B, USER_BOARD.D6_PWM
  DRV0_B: QUAD_2_1_MUX.A_2Y, DC_MOTOR_DRIVER.IN2
  DRV1_A: QUAD_2_1_MUX.A_3Y, DC_MOTOR_DRIVER.IN3
  USR_DRV1A: QUAD_2_1_MUX.A_3B, USER_BOARD.D9_PWM
  N3: QUAD_2_1_MUX.A_3A, CONTROLER_BOARD.D9_PWM
  DRV1_B: QUAD_2_1_MUX.A_4Y, DC_MOTOR_DRIVER.IN4
  USR_DRV1B: QUAD_2_1_MUX.A_4B, USER_BOARD.D10_PWM/SS
  N4: QUAD_2_1_MUX.A_4A, CONTROLER_BOARD.D10_PWM/SS
  N5: DC_MOTOR_DRIVER.OUT1, MOTORS.pin1
  N6: DC_MOTOR_DRIVER.OUT2, MOTORS.pin2
  DRV0_ON: DC_MOTOR_DRIVER.ENA, CONTROLER_BOARD.D7
  DRV1_ON: DC_MOTOR_DRIVER.ENB, CONTROLER_BOARD.D8
  N7: DC_MOTOR_DRIVER.OUT3, MOTORS.pin3
  N8: DC_MOTOR_DRIVER.OUT4, MOTORS.pin4
